// Logisim project M1Solution.circ as structural Verilog: 2 circuits, main circuit main
module main (
  input  WRITE,
  input  READ,
  input  LD_AR,
  input  INC_AR,
  input  CLR_AR,
  input  LD_PC,
  input  [2:0] S2S1S0,
  input  INC_PC,
  input  CLR_PC,
  input  LD_AC,
  input  INC_AC,
  input  CLR_AC,
  input  [3:0] C3C2C1C0,
  input  LD_DR,
  input  INC_DR,
  input  CLR_DR,
  input  LD_TR,
  input  INC_TR,
  input  CLR_TR,
  input  LD_IR
);

  wire CLOCK_out;
  wire [6:0] AR_q, bit_extender_1_out, bit_extender_2_out, PC_q;
  wire [15:0] AC_q, ALU_output, bit_extender_3_out, bit_extender_4_out, DR_q, IR_q, multiplexer_1_out,
       ram_1_data, TR_q;

  Clock CLOCK (.out(CLOCK_out));
  Bit_Extender #(.in_width(16), .out_width(7)) bit_extender_1 (.in(multiplexer_1_out), .out(bit_extender_1_out));
  Bit_Extender #(.in_width(16), .out_width(7)) bit_extender_2 (.in(multiplexer_1_out), .out(bit_extender_2_out));
  ALU ALU (.DR(DR_q), .AC(AC_q), .BUS(multiplexer_1_out), .C3C2C1C0(C3C2C1C0), .OUTPUT(ALU_output));
  Counter #(.width(7), .max('h7f)) AR (
    .load(LD_AR), .D(bit_extender_1_out), .count(INC_AR), .Q(AR_q), .clk(CLOCK_out), .clr(CLR_AR));  // open: carry
  Counter #(.width(7), .max('h7f)) PC (
    .load(LD_PC), .D(bit_extender_2_out), .count(INC_PC), .Q(PC_q), .clk(CLOCK_out), .clr(CLR_PC));  // open: carry
  Counter #(.width(16), .max('hffff)) DR (
    .load(LD_DR), .D(multiplexer_1_out), .count(INC_DR), .Q(DR_q), .clk(CLOCK_out), .clr(CLR_DR));  // open: carry
  Counter #(.width(16), .max('hffff)) TR (
    .load(LD_TR), .D(multiplexer_1_out), .count(INC_TR), .Q(TR_q), .clk(CLOCK_out), .clr(CLR_TR));  // open: carry
  Register #(.width(16)) IR (.D(multiplexer_1_out), .en(LD_IR), .Q(IR_q), .clk(CLOCK_out));  // open: clr
  assign bit_extender_3_out = {{9{1'b0}}, AR_q};  // Bit_Extender bit_extender_3
  assign bit_extender_4_out = {{9{1'b0}}, PC_q};  // Bit_Extender bit_extender_4
  Counter #(.width(16), .max('hffff)) AC (
    .load(LD_AC), .D(ALU_output), .count(INC_AC), .Q(AC_q), .clk(CLOCK_out), .clr(CLR_AC));  // open: carry
  RAM #(.addrWidth(7), .dataWidth(16), .bus("separate")) ram_1 (
    .addr(AR_q), .din(multiplexer_1_out), .data(ram_1_data), .str(WRITE), .clk(CLOCK_out), .ld(READ));  // open: sel, clr
  Multiplexer #(.select(3), .width(16), .enable("false")) multiplexer_1 (
    .in1(bit_extender_3_out), .in2(bit_extender_4_out), .in3(AC_q), .in4(DR_q), .in5(TR_q), .in6(ram_1_data),
    .in7(IR_q), .out(multiplexer_1_out), .sel(S2S1S0));  // open: in0
endmodule

module ALU (
  input  [15:0] DR,
  input  [15:0] AC,
  input  [15:0] BUS,
  input  [3:0] C3C2C1C0,
  output [15:0] OUTPUT
);

  wire [15:0] adder_1_out, adder_2_out, and_1_out, multiplier_1_out, multiplier_2_out, not_1_out, not_2_out;

  Adder #(.width(16)) adder_1 (.a(DR), .b(AC), .out(adder_1_out));  // open: cin, cout
  Adder #(.width(16)) adder_2 (.a(AC), .b(BUS), .out(adder_2_out));  // open: cin, cout
  assign not_1_out = ~AC;  // NOT_Gate not_1, 16 bits wide
  assign not_2_out = ~BUS;  // NOT_Gate not_2, 16 bits wide
  assign and_1_out = DR & AC;  // AND_Gate and_1, 16 bits wide
  Multiplier #(.width(16)) multiplier_1 (.a(DR), .b(AC), .out(multiplier_1_out));  // open: cin, cout
  Multiplier #(.width(16)) multiplier_2 (.a(AC), .b(BUS), .out(multiplier_2_out));  // open: cin, cout
  Multiplexer #(.select(4), .width(16)) multiplexer_1 (
    .in1(DR), .in2(BUS), .in3(adder_1_out), .in4(adder_2_out), .in5(and_1_out), .in6(not_1_out),
    .in7(not_2_out), .in8(multiplier_1_out), .in9(multiplier_2_out), .out(OUTPUT), .sel(C3C2C1C0));  // open: in0, in10, in11, in12, in13, in14, in15, en
endmodule
