// Logisim project Bus.circ as structural Verilog: 2 circuits, main circuit BUS
module BUS (
  input  Store,
  input  in_2,
  input  CLK,
  input  in_4,
  input  in_5,
  input  [2:0] Bus_Select,
  input  in_7,
  input  in_8,
  input  Load,
  input  INC,
  input  in_11,
  input  [3:0] ALU_Select,
  input  Load_2,
  input  in_14,
  input  in_15,
  input  in_16,
  input  in_17,
  input  in_18,
  input  in_19,
  output [15:0] Value_in_Bus
);

  wire not_1_out;
  wire [6:0] AR_q, bit_extender_1_out, bit_extender_2_out, bit_extender_5_out, PC_q;
  wire [15:0] AC_q, ALU_out_5, bit_extender_3_out, bit_extender_4_out, controlled_buffer_1_out, DR_q, IR_q,
       TR_q;

  Bit_Extender #(.in_width(16), .out_width(7)) bit_extender_1 (.in(Value_in_Bus), .out(bit_extender_1_out));
  Bit_Extender #(.in_width(16), .out_width(7)) bit_extender_2 (.in(Value_in_Bus), .out(bit_extender_2_out));
  Counter #(.width(7), .max('h7f)) PC (
    .D(bit_extender_2_out), .count(in_7), .Q(PC_q), .clk(CLK), .clr(in_8));  // open: load, carry
  ALU ALU (.BUS(Value_in_Bus), .DR(DR_q), .AC(AC_q), .in_3(ALU_Select), .out_5(ALU_out_5));
  assign controlled_buffer_1_out = Store ? Value_in_Bus : 16'bz;  // Controlled_Buffer controlled_buffer_1
  assign bit_extender_3_out = {{9{1'b0}}, AR_q};  // Bit_Extender bit_extender_3
  Counter #(.width(7), .max('h7f)) AR (
    .D(bit_extender_1_out), .count(in_4), .Q(AR_q), .clk(CLK), .clr(in_5));  // open: load, carry
  assign bit_extender_4_out = {{9{1'b0}}, PC_q};  // Bit_Extender bit_extender_4
  Counter #(.width(16), .max('hffff)) AC (
    .load(Load), .D(ALU_out_5), .count(INC), .Q(AC_q), .clk(CLK), .clr(in_11));  // open: carry
  Counter #(.width(16), .max('hffff)) DR (
    .load(Load_2), .D(Value_in_Bus), .count(in_14), .Q(DR_q), .clk(CLK), .clr(in_15));  // open: carry
  Counter #(.width(16), .max('hffff)) TR (
    .D(Value_in_Bus), .count(in_16), .Q(TR_q), .clk(CLK), .clr(in_17));  // open: load, carry
  Counter #(.width(16), .max('hffff)) IR (
    .D(Value_in_Bus), .count(in_18), .Q(IR_q), .clk(CLK), .clr(in_19));  // open: load, carry
  Bit_Extender #(.in_width(16), .out_width(7)) bit_extender_5 (.in(bit_extender_3_out), .out(bit_extender_5_out));
  not not_1 (not_1_out, Store);
  RAM #(.addrWidth(7), .dataWidth(16)) ram_1 (
    .addr(bit_extender_5_out), .data(controlled_buffer_1_out), .clk(CLK), .ld(not_1_out), .clr(in_2));  // open: sel
  Multiplexer #(.select(3), .width(16)) multiplexer_1 (
    .in1(bit_extender_3_out), .in2(bit_extender_4_out), .in3(AC_q), .in4(DR_q), .in5(TR_q),
    .in6(controlled_buffer_1_out), .in7(IR_q), .out(Value_in_Bus), .sel(Bus_Select));  // open: in0, en
endmodule

module ALU (
  input  [15:0] BUS,
  input  [15:0] DR,
  input  [3:0] in_3,
  input  [15:0] AC,
  output [15:0] out_5
);

  wire [15:0] adder_1_out, adder_2_out, and_1_out, multiplier_1_out, multiplier_2_out, not_1_out, not_2_out;

  Adder #(.width(16)) adder_1 (.a(DR), .b(AC), .out(adder_1_out));  // open: cin, cout
  Adder #(.width(16)) adder_2 (.a(AC), .b(BUS), .out(adder_2_out));  // open: cin, cout
  assign and_1_out = DR & AC;  // AND_Gate and_1, 16 bits wide
  assign not_1_out = ~AC;  // NOT_Gate not_1, 16 bits wide
  Multiplier #(.width(16)) multiplier_1 (.a(DR), .b(AC), .out(multiplier_1_out));  // open: cin, cout
  Multiplier #(.width(16)) multiplier_2 (.a(AC), .b(BUS), .out(multiplier_2_out));  // open: cin, cout
  assign not_2_out = ~BUS;  // NOT_Gate not_2, 16 bits wide
  Multiplexer #(.select(4), .width(16)) multiplexer_1 (
    .in1(DR), .in2(BUS), .in3(adder_1_out), .in4(adder_2_out), .in5(and_1_out), .in6(not_1_out),
    .in7(not_2_out), .in8(multiplier_1_out), .in9(multiplier_2_out), .out(out_5), .sel(in_3));  // open: in0, in10, in11, in12, in13, in14, in15, en
endmodule
