// Logisim project Team64_Milestone2.circ as structural Verilog: 3 circuits, main circuit main
module main (
  input  INC_AR,
  input  CLR_AR,
  input  CLR_PC,
  input  INC_AC,
  input  CLR_AC,
  input  CLR_DR,
  input  LD_TR,
  input  INC_TR,
  input  CLR_TR
);

  wire AC_LD, AR_LD, CLK_out, DR_INC, DR_LD, IR_LD, MEM_R, MEM_W, PC_INC, PC_LD;
  wire [2:0] S2S1S0;
  wire [3:0] C3C2C1C0;
  wire [6:0] AR_q, bit_extender_1_out, bit_extender_2_out, PC_q;
  wire [15:0] AC_q, alu_1_output, bit_extender_3_out, bit_extender_4_out, DR, IR, multiplexer_1_out,
       ram_1_data, TR_q;

  Clock CLK (.out(CLK_out));
  CU cu_1 (
    .CLK(CLK_out), .IR(IR), .DR(DR), .DR_INC(DR_INC), .IR_LD(IR_LD), .MEM_W(MEM_W), .MEM_R(MEM_R),
    .DR_LD(DR_LD), .PC_LD(PC_LD), .AR_LD(AR_LD), .AC_LD(AC_LD), .ALU(C3C2C1C0), .BUS(S2S1S0), .PC_INC(PC_INC));
  Bit_Extender #(.in_width(16), .out_width(7)) bit_extender_1 (.in(multiplexer_1_out), .out(bit_extender_1_out));
  Bit_Extender #(.in_width(16), .out_width(7)) bit_extender_2 (.in(multiplexer_1_out), .out(bit_extender_2_out));
  ALU alu_1 (.DR(DR), .AC(AC_q), .BUS(multiplexer_1_out), .C3C2C1C0(C3C2C1C0), .OUTPUT(alu_1_output));
  Counter #(.width(7), .max('h7f)) AR (
    .load(AR_LD), .D(bit_extender_1_out), .count(INC_AR), .Q(AR_q), .clk(CLK_out), .clr(CLR_AR));  // open: carry
  Counter #(.width(7), .max('h7f)) PC (
    .load(PC_LD), .D(bit_extender_2_out), .count(PC_INC), .Q(PC_q), .clk(CLK_out), .clr(CLR_PC));  // open: carry
  Counter #(.width(16), .max('hffff)) u_DR (
    .load(DR_LD), .D(multiplexer_1_out), .count(DR_INC), .Q(DR), .clk(CLK_out), .clr(CLR_DR));  // open: carry
  Counter #(.width(16), .max('hffff)) TR (
    .load(LD_TR), .D(multiplexer_1_out), .count(INC_TR), .Q(TR_q), .clk(CLK_out), .clr(CLR_TR));  // open: carry
  Register #(.width(16)) u_IR (.D(multiplexer_1_out), .en(IR_LD), .Q(IR), .clk(CLK_out));  // open: clr
  assign bit_extender_3_out = {{9{1'b0}}, AR_q};  // Bit_Extender bit_extender_3
  assign bit_extender_4_out = {{9{1'b0}}, PC_q};  // Bit_Extender bit_extender_4
  Counter #(.width(16), .max('hffff)) AC (
    .load(AC_LD), .D(alu_1_output), .count(INC_AC), .Q(AC_q), .clk(CLK_out), .clr(CLR_AC));  // open: carry
  RAM #(.addrWidth(7), .dataWidth(16), .bus("separate")) ram_1 (
    .addr(AR_q), .din(multiplexer_1_out), .data(ram_1_data), .str(MEM_W), .clk(CLK_out), .ld(MEM_R));  // open: sel, clr
  Multiplexer #(.select(3), .width(16), .enable("false")) multiplexer_1 (
    .in1(bit_extender_3_out), .in2(bit_extender_4_out), .in3(AC_q), .in4(DR), .in5(TR_q), .in6(ram_1_data),
    .in7(IR), .out(multiplexer_1_out), .sel(S2S1S0));  // open: in0
endmodule

module ALU (
  input  [15:0] DR,
  input  [15:0] AC,
  input  [15:0] BUS,
  input  [3:0] C3C2C1C0,
  output [15:0] OUTPUT
);

  wire [15:0] adder_1_out, adder_2_out, and_1_out, multiplier_1_out, multiplier_2_out, not_1_out, not_2_out;

  Adder #(.width(16)) adder_1 (.a(DR), .b(AC), .out(adder_1_out));  // open: cin, cout
  Adder #(.width(16)) adder_2 (.a(AC), .b(BUS), .out(adder_2_out));  // open: cin, cout
  assign not_1_out = ~AC;  // NOT_Gate not_1, 16 bits wide
  assign not_2_out = ~BUS;  // NOT_Gate not_2, 16 bits wide
  assign and_1_out = DR & AC;  // AND_Gate and_1, 16 bits wide
  Multiplier #(.width(16)) multiplier_1 (.a(DR), .b(AC), .out(multiplier_1_out));  // open: cin, cout
  Multiplier #(.width(16)) multiplier_2 (.a(AC), .b(BUS), .out(multiplier_2_out));  // open: cin, cout
  Multiplexer #(.select(4), .width(16), .enable("false")) multiplexer_1 (
    .in1(DR), .in2(BUS), .in3(adder_1_out), .in4(adder_2_out), .in5(and_1_out), .in6(not_1_out),
    .in7(not_2_out), .in8(multiplier_1_out), .in9(multiplier_2_out), .out(OUTPUT), .sel(C3C2C1C0));  // open: in0, in10, in11, in12, in13, in14, in15
endmodule

module CU (
  input  CLK,
  input  [15:0] IR,
  input  [15:0] DR,
  output DR_INC,
  output IR_LD,
  output MEM_W,
  output MEM_R,
  output DR_LD,
  output PC_LD,
  output AR_LD,
  output AC_LD,
  output [3:0] ALU,
  output [2:0] BUS,
  output PC_INC
);

  wire and_14_out, CLR_SC, D0, D0T3, D0T4, D1, D1T3, D1T4, D2, D2T3, D2T4, D3, D3T3, D4, D5, D5T3, D5T4, D6,
       D6T3, D6T5, D7, d_ff_1_q, nor_1_out, or_2_out, T0, T2, T3, T4, T5, T6, T7, T8, T9, T10, T11, T12, T13,
       T14, T15;
  wire [3:0] SC_q;

  Counter #(.width(4), .max('hf)) SC (.Q(SC_q), .clk(CLK), .clr(d_ff_1_q));  // open: load, D, count, carry
  D_Flip_Flop d_ff_1 (.clk(CLK), .D(CLR_SC), .Q(d_ff_1_q));  // open: Qn, preset, en, reset
  Decoder #(.select(3), .enable("false")) decoder_1 (
    .out0(D0), .out1(D1), .out2(D2), .out3(D3), .out4(D4), .out5(D5), .out6(D6), .out7(D7), .sel(IR[14:12]));
  Decoder #(.select(4), .enable("false")) decoder_2 (
    .out0(T0), .out1(IR_LD), .out2(T2), .out3(T3), .out4(T4), .out5(T5), .out6(T6), .out7(T7), .out8(T8),
    .out9(T9), .out10(T10), .out11(T11), .out12(T12), .out13(T13), .out14(T14), .out15(T15), .sel(SC_q));
  or or_1 (DR_LD, D0T3, D1T3, D2T3, D5T3, D6T3);
  and and_1 (D0T4, D0, T4);
  and and_2 (D1T4, D1, T4);
  and and_3 (D2T4, D2, T4);
  and and_4 (D3T3, D3, T3);
  and and_5 (PC_LD, D4, T3);
  and and_6 (D5T3, D5, T3);
  and and_7 (D6T5, D6, T5);
  and and_8 (DR_INC, D6, T4);
  or or_2 (or_2_out, IR_LD, DR_LD);
  Priority_Encoder priority_encoder_1 (
    .in1(PC_LD), .in2(T0), .in3(D3T3), .in4(D6T5), .in6(or_2_out), .in7(T2), .out(BUS));  // open: in0, in5, en_in, gs, en_out
  or or_3 (CLR_SC, D0T4, D1T4, D2T4, D3T3, PC_LD, D5T4, D6T5);
  and and_9 (D0T3, D0, T3);
  and and_10 (D1T3, D1, T3);
  and and_11 (D2T3, D2, T3);
  and and_12 (D6T3, D6, T3);
  and and_13 (D5T4, D5, T4);
  Priority_Encoder #(.select(4)) priority_encoder_2 (
    .in1(D2T4), .in3(D1T4), .in5(D0T4), .in8(D5T4), .out(ALU));  // open: in0, in2, in4, in6, in7, in9, in10, in11, in12, in13, in14, in15, gs, en_out, en_in
  nor nor_1 (nor_1_out, DR[0], DR[1], DR[2], DR[3], DR[4], DR[5], DR[6], DR[7], DR[8], DR[9], DR[10], DR[11], DR[12], DR[13], DR[14], DR[15]);
  or or_4 (AC_LD, D0T4, D1T4, D2T4, D5T4);
  and and_14 (and_14_out, D6T5, nor_1_out);
  or or_5 (MEM_W, D6T5, D3T3);
  or or_6 (MEM_R, IR_LD, DR_LD);
  or or_7 (AR_LD, T0, T2);
  or or_8 (PC_INC, and_14_out, IR_LD);

  // Other names for the same wires on the sheet: D4T3 = PC_LD; D6T4 = DR_INC; Address[11:0] = IR[11:0]; T1 = IR_LD;
  //   T3_1 = DR_LD
endmodule
